# Fritzing sketch Schaltplan_v2 (saved by Fritzing 0.9.3b)
circuit board: 6.90506cm x 5.39633cm
breadboards: 2

parts:
  PB = Pushbutton [package="[THT]"]
  R3 = Resistor [tolerance=±5% power=0.25 resistance=2.2k package=THT]
  R6 = Resistor [tolerance=±5% power=0.25 resistance=220 package=THT]
  R5 = Resistor [tolerance=±5% power=0.25 resistance=220 package=THT]
  R4 = Resistor [tolerance=±5% power=0.25 resistance=220 package=THT]
  AB = Pushbutton [package="[THT]"]
  R1 = Resistor [tolerance=±5% power=0.25 resistance=10k package=THT]
  DIP-Switch = DIP Switch 8 Position [package=dipswitch-08]
  Fototransistor = LTR-301 [package=ltr-301]
  Feuchtigkeitssensor = Soil Moisture Sensor
  R2 = Resistor [tolerance=±5% power=0.25 resistance=10k package=THT]
  Adafruit_BME688 = Adafruit BME680
  Arduino_Nano_33_BLE = Arduino Nano 33 BLE Sense
  R7 = Bussed8 Resistor-8 (SIP-9) [tolerance=±5% resistance=10k package=SIP-9]
  Piezo-Buzzer = Piezo Speaker
  RBG-LED = RGB LED (com. cathode, rgb) [package="5 mm [THT]"]

nets:
  N1: PB.Pin_1, PB.Pin_2, R2.Pin_1, Arduino_Nano_33_BLE.A1
  GND: PB.Pin_3, PB.Pin_4, R3.Pin_1, AB.Pin_3, AB.Pin_4, DIP-Switch.1, DIP-Switch.2, DIP-Switch.3, DIP-Switch.4, DIP-Switch.5, DIP-Switch.6, DIP-Switch.7, DIP-Switch.8, Feuchtigkeitssensor.GND, Adafruit_BME688.GND, Arduino_Nano_33_BLE.GND, Arduino_Nano_33_BLE.A7, Piezo-Buzzer.pin1, RBG-LED.common_cathode
  N2: R3.Pin_0, Fototransistor.E, Arduino_Nano_33_BLE.A3
  N3: R6.Pin_0, RBG-LED.red_anode
  N4: R6.Pin_1, Arduino_Nano_33_BLE.D10~
  N5: R5.Pin_0, RBG-LED.green_anode
  N6: R5.Pin_1, Arduino_Nano_33_BLE.D11/MOSI, Arduino_Nano_33_BLE.+5V
  N7: R4.Pin_0, RBG-LED.blue_anode
  N8: R4.Pin_1, Arduino_Nano_33_BLE.D12~/MISO
  N9: AB.Pin_1, AB.Pin_2, R1.Pin_1, Arduino_Nano_33_BLE.A0
  VCC: R1.Pin_0, Fototransistor.C, Feuchtigkeitssensor.VCC, R2.Pin_0, Adafruit_BME688.VCC, Arduino_Nano_33_BLE.3V3, R7.Pin_0
  N10: DIP-Switch.9, Arduino_Nano_33_BLE.D9~, R7.Pin_8
  N11: DIP-Switch.10, Arduino_Nano_33_BLE.D8, R7.Pin_7
  N12: DIP-Switch.11, Arduino_Nano_33_BLE.D7, R7.Pin_6
  N13: DIP-Switch.12, Arduino_Nano_33_BLE.D6~, R7.Pin_5
  N14: DIP-Switch.13, Arduino_Nano_33_BLE.D5~, R7.Pin_4
  N15: DIP-Switch.14, Arduino_Nano_33_BLE.D4, R7.Pin_3
  N16: DIP-Switch.15, Arduino_Nano_33_BLE.D3~, R7.Pin_2
  N17: DIP-Switch.16, Arduino_Nano_33_BLE.D2, R7.Pin_1
  N18: Feuchtigkeitssensor.SIG, Arduino_Nano_33_BLE.A2
  N19: Adafruit_BME688.SDI/SDA, Arduino_Nano_33_BLE.A4
  N20: Adafruit_BME688.SCK/SCL, Arduino_Nano_33_BLE.A5
  N21: Arduino_Nano_33_BLE.A6, Piezo-Buzzer.pin2

notes:
  Hygrosensor
  Fototransistor
  Pairing Button
  R = 220 Ohm
  R = 2,2 kOhm
  R = 10 kOhm
  Acknowledgment

custom parts:
  Arduino Nano 33 BLE Sense: The Nano 33 BLE Sense (without headers) is Arduino’s 3.3V AI enabled board in the smallest available form factor: 45x18mm! The Arduino Nano 33 BLE Sense is a completely new board on a well-known form factor. It comes with a series of embedded sensors: 9 axis inertial sensor: what makes this board ideal for wearable devices humidity, and temperature sensor: to get highly accurate measurements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
  Bussed8 Resistor-8 (SIP-9): A resistor array is a single package which contains more than one resistor. They are typically used for convenience when several resistors are needed together in the same place in a circuit.
